# Fritzing sketch schema (saved by Fritzing 0.9.3b)
breadboards: 1

parts:
  U1 = 74HC595 [package="DIP16 [THT]"]
  7_Segment1 = 7 Segment Display
  Q1 = NPN-Transistor [package="TO92 [THT]"]
  Q2 = NPN-Transistor [package="TO92 [THT]"]
  Q3 = NPN-Transistor [package="TO92 [THT]"]
  Part1 = Arduino Uno (Rev3) - ICSP
  Q4 = NPN-Transistor [package="TO92 [THT]"]
  Q5 = NPN-Transistor [package="TO92 [THT]"]
  Q6 = NPN-Transistor [package="TO92 [THT]"]
  Q7 = NPN-Transistor [package="TO92 [THT]"]
  hc-sr1 = hc-sr04

nets:
  N1: U1.Q1, Q4.C
  N2: U1.Q2, Q6.C
  N3: U1.Q3, Q7.C
  N4: U1.Q4, Q1.C
  N5: U1.Q5, Q2.C
  N6: U1.Q6, Q5.C
  GND: U1.GND, U1.OE, Q1.E, Q2.E, Q3.E, Part1.GND, Q4.E, Q5.E, Q6.E, Q7.E, hc-sr1.GND
  VCC: U1.MR, U1.VCC, 7_Segment1.common_anode#3, 7_Segment1.common_anode#5, 7_Segment1.common_anode#11, 7_Segment1.common_anode#16, Part1.5V, hc-sr1.VCC
  N7: U1.SH_CP, Part1.D10_PWM/SS
  N8: U1.ST_CP, Part1.D9_PWM
  N9: U1.DS, Part1.D8
  N10: U1.Q0, Q3.C
  N11: 7_Segment1.Segment_A, Q3.B
  N12: 7_Segment1.Segment_F, Q2.B
  N13: 7_Segment1.Segment_E, Q1.B
  N14: 7_Segment1.Segment_D, Q7.B
  N15: 7_Segment1.common_anode#12, Q6.B
  N16: 7_Segment1.Segment_G, Q5.B
  N17: 7_Segment1.Segment_B, Q4.B
  N18: Part1.ICSP_MOSI, Part1.D11_PWM/MOSI, hc-sr1.Trig
  N19: Part1.D12/MISO, hc-sr1.Echo
