# Fritzing sketch schema (saved by Fritzing 0.9.3b)
breadboards: 1

parts:
  Part1 = Arduino Uno (Rev3) - ICSP
  LED2 = smd LED [color="Red (633nm)" package="0805 [SMD]"]
  R1 = Resistor [tolerance=±5% resistance=220 package="2010 [SMD]"]
  LED3 = smd LED [color="Red (633nm)" package="0805 [SMD]"]
  R2 = Resistor [tolerance=±5% resistance=220 package="2010 [SMD]"]
  LED4 = smd LED [color="Red (633nm)" package="0805 [SMD]"]
  R3 = Resistor [tolerance=±5% resistance=220 package="2010 [SMD]"]
  LED5 = smd LED [color="Red (633nm)" package="0805 [SMD]"]
  R4 = Resistor [tolerance=±5% resistance=220 package="2010 [SMD]"]
  LED6 = smd LED [color="Red (633nm)" package="0805 [SMD]"]
  R5 = Resistor [tolerance=±5% resistance=220 package="2010 [SMD]"]
  LED7 = smd LED [color="Red (633nm)" package="0805 [SMD]"]
  R6 = Resistor [tolerance=±5% resistance=220 package="2010 [SMD]"]
  LED8 = smd LED [color="Red (633nm)" package="0805 [SMD]"]
  R7 = Resistor [tolerance=±5% resistance=220 package="2010 [SMD]"]
  LED9 = smd LED [color="Red (633nm)" package="0805 [SMD]"]
  R8 = Resistor [tolerance=±5% resistance=220 package="2010 [SMD]"]
  U1 = 74HC595 [package="DIP16 [THT]"]

nets:
  5V: Part1.5V, U1.MR, U1.VCC
  N1: Part1.D8, U1.DS
  N2: Part1.D9_PWM, U1.ST_CP
  N3: Part1.D10_PWM/SS, U1.SH_CP
  GND: Part1.GND, LED2.cathode, LED3.cathode, LED4.cathode, LED5.cathode, LED6.cathode, LED7.cathode, LED8.cathode, LED9.cathode, U1.GND, U1.OE
  N4: LED2.anode, R1.Pin_1
  N5: R1.Pin_0, U1.Q7
  N6: LED3.anode, R2.Pin_1
  N7: R2.Pin_0, U1.Q6
  N8: LED4.anode, R3.Pin_1
  N9: R3.Pin_0, U1.Q5
  N10: LED5.anode, R4.Pin_1
  N11: R4.Pin_0, U1.Q4
  N12: LED6.anode, R5.Pin_1
  N13: R5.Pin_0, U1.Q3
  N14: LED7.anode, R6.Pin_1
  N15: R6.Pin_0, U1.Q2
  N16: LED8.anode, R7.Pin_1
  N17: R7.Pin_0, U1.Q1
  N18: LED9.anode, R8.Pin_1
  N19: R8.Pin_0, U1.Q0
