# Fritzing sketch schema (saved by Fritzing 0.9.3b)
breadboards: 1

parts:
  Part1 = Arduino Uno (Rev3) - ICSP
  Q1 = TRANSISTOR_NPN [package=to-92]
  Q2 = TRANSISTOR_NPN [package=to-92]
  Q3 = TRANSISTOR_NPN [package=to-92]
  Q4 = TRANSISTOR_NPN [package=to-92]
  Q5 = TRANSISTOR_NPN [package=to-92]
  Q6 = TRANSISTOR_NPN [package=to-92]
  Q7 = TRANSISTOR_NPN [package=to-92]
  R1 = Resistor [tolerance=±5% resistance=220 package="0402 [SMD]"]
  R2 = Resistor [tolerance=±5% resistance=220 package="0402 [SMD]"]
  R3 = Resistor [tolerance=±5% resistance=220 package="0402 [SMD]"]
  R4 = Resistor [tolerance=±5% resistance=220 package="0402 [SMD]"]
  R5 = Resistor [tolerance=±5% resistance=220 package="0402 [SMD]"]
  R6 = Resistor [tolerance=±5% resistance=220 package="0402 [SMD]"]
  R7 = Resistor [tolerance=±5% resistance=220 package="0402 [SMD]"]
  U1 = 7-SEGMENT-DISPLAY-1_-RED [package=7-segment-1_pth]

nets:
  N1: Part1.GND, Q1.C, Q2.C, Q3.C, Q4.C, Q5.C, Q6.C, Q7.C
  N2: Part1.5V, U1.G1
  N3: Part1.D8, R4.Pin_0
  N4: Part1.D9_PWM, R5.Pin_0
  N5: Part1.D3_PWM, R7.Pin_0
  N6: Part1.D4, R6.Pin_0
  N7: Part1.D5_PWM, R1.Pin_0
  N8: Part1.D6_PWM, R2.Pin_0
  N9: Part1.D7, R3.Pin_0
  N10: Q1.E, U1.B
  N11: Q1.B, R7.Pin_1
  N12: Q2.E, U1.G
  N13: Q2.B, R6.Pin_1
  N14: Q3.E, U1.F
  N15: Q3.B, R1.Pin_1
  N16: Q4.E, U1.A
  N17: Q4.B, R2.Pin_1
  N18: Q5.E, U1.E
  N19: Q5.B, R3.Pin_1
  N20: Q6.E, U1.C
  N21: Q6.B, R4.Pin_1
  N22: Q7.E, U1.D
  N23: Q7.B, R5.Pin_1
